# Fritzing sketch Diagrama Arduino (2) (saved by Fritzing 0.9.3b)
breadboards: 1

parts:
  U1 = XBee
  Componente2 = Arduino Nano (Rev3.0)
  IC1 = H-Bridge [package=THT]
  VCC1 = Battery [part_number=7.8V]
  VCC2 = Battery block 9V
  M1 = DC Motor
  M2 = DC Motor
  C1 = Ceramic Capacitor [capacitance=100nF package="100 mil [THT, multilayer]"]  # not connected
  C2 = Ceramic Capacitor [capacitance=100nF package="100 mil [THT, multilayer]"]
  U4 = Voltage Regulator - 5V [package="TO220 [THT]"]
  IC3 = H-Bridge [package=THT]
  M3 = DC Motor

nets:
  VCC: U1.VCC, Componente2.3V3
  N1: U1.pin2, Componente2.D0/RX
  N2: U1.pin3, Componente2.D1/TX
  GND: U1.GND, Componente2.GND, IC1.GND2, VCC1.-, IC3.GND2
  N3: Componente2.D3, IC3.2A
  N4: Componente2.D4, IC3.1A
  N5: Componente2.D5, IC1.2A
  N6: Componente2.D6, IC1.1A
  N7: Componente2.D9, IC1.3A
  N8: Componente2.D10, IC1.4A
  N9: Componente2.VIN, VCC1.+
  N10: IC1.1_2EN, VCC2.+, U4.input_voltage
  N11: IC1.1Y, M1.pin_2
  GND1: IC1.GND1, VCC2.-, C2.0, IC3.GND1
  N12: IC1.2Y, M1.pin_1
  N13: IC1.3Y, M2.pin_1
  N14: IC1.4Y, M2.pin_2
  N15: U4.output_voltage, IC3.1_2EN
  N16: IC3.1Y, M3.pin_2
  N17: IC3.2Y, M3.pin_1
